# Fritzing sketch schema progetto mod (saved by Fritzing 0.9.6b)
breadboards: 1

parts:
  L298N1 = L298N DC motor driver
  Componente1 = Arduino Uno (Rev3)
  M1 = DC Motor
  M2 = DC Motor
  HC-SR04_Sensor_1 = HC-SR04 Ultrasonic Distance Sensor
  Esp32-cam1 = ESP32-Cam
  U1 = POT [package=pot_mammoth]
  U2 = POT [package=pot_mammoth]
  U3 = POT [package=pot_mammoth]

nets:
  N1: L298N1.OUT1, M1.pin_2
  N2: L298N1.OUT2, M1.pin_1
  N3: L298N1.OUT3, M2.pin_1
  N4: L298N1.OUT4, M2.pin_2
  GND: L298N1.GND, HC-SR04_Sensor_1.GND, Esp32-cam1.GND
  5V: L298N1.5V, HC-SR04_Sensor_1.VCC, Esp32-cam1.5V
  N5: L298N1.ENA, Componente1.D11_PWM/MOSI
  N6: L298N1.ENB, Componente1.D9_PWM
  N7: L298N1.IN1, Componente1.D13/SCK
  N8: L298N1.IN2, Componente1.D12/MISO
  N9: L298N1.IN3, Componente1.D10_PWM/SS
  N10: L298N1.IN4, Componente1.D8
  N11: Componente1.A0, U1.A
  N12: Componente1.A1, U2.A
  N13: Componente1.A2, U3.A
  N14: Componente1.A4/SDA, Esp32-cam1.GPIO_15
  N15: Componente1.A5/SCL, Esp32-cam1.GPIO_14
  N16: Componente1.5V, U1.S, U2.E, U3.S
  N17: HC-SR04_Sensor_1.TRIG, Esp32-cam1.GPIO_13
  N18: HC-SR04_Sensor_1.ECHO, Esp32-cam1.GPIO_2
  N19: U1.E, U2.S, U3.E

notes:
  Alimenentazione Primaria arduino
  12 volt DC
  Distanziometro
  Linea IN - Linea OUT comunicazione Seriale
  Alimnentzione L298N
  12 volt DC
  Alimentazione
  5v DC out L298N
  ESP -
  distanz.
  5V DC
  comunicazione con potenziometri
  Potenziometro di regolazione
  Kv1 - kv2 - Delay

custom parts:
  L298N DC motor driver: 2x DC motor driver with 78M05 positive voltage regulator (7..35 V) L298N: max 46 V, 2 A Set 5 V Enable jumper to enable 5 V regultor (needed for the L298N) and +5 V output at screw terminal or supply external +5 V at screw terminal Set ENA and/or ENB to +5 V to enable motor permanently or supply ENA and/or ENB with PWM signal IN1 and IN2 set rotation directory for motor A (OUT1/OUT2) IN2 and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

// code stored in the sketch: arduinoschetch.ino
/*
   L298N pilotare un motore DC con Arduino
   Programmino per imparare il funzionamento del Modulo L298N e del suo utilizzo con Arduino

   Autore  : Andrea Lombardo
   Web     : http://www.lombardoandrea.com
   Post    : http://bit.ly/L298N-ARDUINO-MOTOREDC
   Git     : https://github.com/AndreaLombardo/Arduino-L298N-Motore-DC
*/

//definizione dei pin
static int pinAcceleratore = A0; //pin analogico deputato a leggere i valori del potenziometro
static int mDXavanti = 12; //pin digitale per determinare gli stati logici da inviare al modulo
static int mDXdietro = 13; //pin digitale per determinare gli stati logici da inviare al modulo
static int pinPotenzaR = 11; //pin digitale tramite il quale inviare un segnale di tipo PWM tramite la funzione analgWrite()
static int mSXdietro = 8; //pin digitale per determinare gli stati logici da inviare al modulo
static int mSXavanti = 10; //pin digitale per determinare gli stati logici da inviare al modulo
static int pinPotenzaL = 9; //pin digitale tramite il quale inviare un segnale di tipo PWM tramite la funzione analgWrite()


//variabili usate per gestire e mostrare i valori di operaizone
int accelerazione;  //valore letto dal pin A0
int potenza;  //valore in uscita dal pin 11

//Distanziometro
const int trigPin = 2;
const int echoPin = 3;

const int in1esp = A5; // analog 
const int in2esp = 7; // solo digital

long duration;
int distance;

int inesp;


void setup() {
  //inizializzo la comunicazione seriale cosi da mostrare i valori nel Mointor Seriale
  pinMode(trigPin, OUTPUT);
  pinMode(echoPin, INPUT);
  Serial.begin(115200);

  //inizializzo variabili
  accelerazione = 0;
  potenza = 0;

  //definisco tipologia pin
  pinMode(pinAcceleratore, INPUT); //input in quanto legge il valore analogico del pin A0
  pinMode(mDXavanti, OUTPUT); //output perche' definisce lo stato logico del pin IN1 del modulo L298N
  pinMode(mDXdietro, OUTPUT); //output perche' definisce lo stato logico del pin IN2 del modulo L298N
  pinMode(pinPotenzaR, OUTPUT);  //output perche' definisce il valore PWM del pin EN1 del modulo L298N
  pinMode(mSXdietro, OUTPUT); //output perche' definisce lo stato logico del pin IN1 del modulo L298N
  pinMode(mSXavanti, OUTPUT); //output perche' definisce lo stato logico del pin IN2 del modulo L298N
  pinMode(pinPotenzaL, OUTPUT);  //output perche' definisce il valore PWM del pin EN1 del modulo L298N

  pinMode(in1esp, INPUT);
  pinMode(in2esp, INPUT);

  //pullDown sensore pinAcceleratore
  digitalWrite(pinAcceleratore, LOW);

  //Definisco il senso di marcia del motore
  /*
    mA |   mB  | Evento
    -----|-------|----------------------
    LOW  | LOW   | fermo
    LOW  | HIGH  | Movimento in un senso
    HIGH | LOW   | Movimento senso opposto
    HIGH | HIGH  | Fermo
  */

 digitalWrite(mDXavanti, LOW);
    digitalWrite(mDXdietro, LOW);
    digitalWrite(mSXdietro, LOW);
    digitalWrite(mSXavanti, LOW);

 // digitalWrite(in1esp, LOW);
  digitalWrite(in2esp, LOW);
}





void loop() {
  //Distanziometro
  digitalWrite(trigPin, LOW);
  delayMicroseconds(2);
  digitalWrite(trigPin, HIGH);
  delayMicroseconds(10);
  digitalWrite(trigPin, LOW);
  duration = pulseIn(echoPin, HIGH);
  distance = duration * 0.034 / 2;
  //Serial.print("Distance: ");
  inesp = analogRead(A5); // il pin 6 analog 
  Serial.println(inesp);
  Serial.println("");
 if(inesp != 0 ){
 // if (digitalRead(in1esp) == HIGH) { // va a destra
    
    
    digitalWrite(mDXavanti, LOW);
    digitalWrite(mDXdietro, HIGH);
    digitalWrite(mSXdietro, LOW);
    digitalWrite(mSXavanti, HIGH);
    digitalWrite(in1esp, LOW);
  //}
  /*
  else if (digitalRead(in2esp) == HIGH) { // va a sinistra
    Serial.println(in2esp);
    digitalWrite(mDXavanti, HIGH);
    digitalWrite(mDXdietro, LOW);
    digitalWrite(mSXdietro, HIGH);
    digitalWrite(mSXavanti, LOW);
    digitalWrite(in2esp, LOW);
  }
  */
 }else{
   if (distance < 15 || distance > 1500) { // resta fermo
    digitalWrite(mDXavanti, LOW);
    digitalWrite(mDXdietro, LOW);
    digitalWrite(mSXdietro, LOW);
    digitalWrite(mSXavanti, LOW);
  }
  
  
  else if (distance > 30 && distance < 1500) { // avanti
    digitalWrite(mDXavanti, HIGH);
    digitalWrite(mDXdietro, LOW);
    digitalWrite(mSXdietro, LOW);
    digitalWrite(mSXavanti, HIGH);
  }
  else if (distance < 35) { // va indietro
    digitalWrite(mDXavanti, LOW);
    digitalWrite(mDXdietro, HIGH);
    digitalWrite(mSXdietro, HIGH);
    digitalWrite(mSXavanti, LOW);
  }
 }
  //Serial.println(distance);
  //fine distanziometro
  //leggo il valore analogico del potenziometro sul pin A0.
  //accelerazione =analogRead(pinAcceleratore);
  accelerazione = 1024;

  /*
    Il range dei valori analogici e' da 0 a 1024 mentre il range dei valori PWM  e' da 0 a 255
    per mantenere questa proporzionalita' eseguo la mappatura dei valori
  */
  potenza = map(accelerazione, 0, 1024, 0, 255);
/*
  //Invio i dati letti al Monitro seriale, cosi da poterli vedere a video
  Serial.print("Accelerazione = ");
  Serial.print(accelerazione);
  Serial.print(" - potenza = ");
  Serial.println(potenza);
*/
  //invio costantemente il valore PWM della potenza in modo da far variare la velocita' del motore in base alla posizione del potenziometro
  analogWrite(pinPotenzaR, potenza);
  analogWrite(pinPotenzaL, potenza);
}
